# Fritzing sketch Schematic Diagram (saved by Fritzing 0.9.3b)

parts:
  LED1 = LED - 5mm [color="Red (633nm)" package="5 mm [THT]"]
  LED2 = LED - 5mm [color="Red (633nm)" package="5 mm [THT]"]
  Part1 = Arduino Mega 2560 (Rev3)
  LED4 = LED - 5mm [color="Red (633nm)" package="5 mm [THT]"]
  LED5 = LED - 5mm [color="Red (633nm)" package="5 mm [THT]"]
  LED6 = LED - 5mm [color="Red (633nm)" package="5 mm [THT]"]
  LED7 = LED - 5mm [color="Red (633nm)" package="5 mm [THT]"]
  LED8 = LED - 5mm [color="Red (633nm)" package="5 mm [THT]"]
  LED9 = LED - 5mm [color="Red (633nm)" package="5 mm [THT]"]
  LED10 = LED - 5mm [color="Red (633nm)" package="5 mm [THT]"]
  LED11 = LED - 5mm [color="Red (633nm)" package="5 mm [THT]"]
  LED12 = LED - 5mm [color="Red (633nm)" package="5 mm [THT]"]
  LED13 = LED - 5mm [color="Red (633nm)" package="5 mm [THT]"]
  LED14 = LED - 5mm [color="Red (633nm)" package="5 mm [THT]"]
  LED15 = LED - 5mm [color="Red (633nm)" package="5 mm [THT]"]
  LED16 = LED - 5mm [color="Red (633nm)" package="5 mm [THT]"]
  LED17 = LED - 5mm [color="Red (633nm)" package="5 mm [THT]"]
  LED18 = LED - 5mm [color="Red (633nm)" package="5 mm [THT]"]
  LED19 = LED - 5mm [color="Red (633nm)" package="5 mm [THT]"]
  LED20 = LED - 5mm [color="Red (633nm)" package="5 mm [THT]"]
  LED21 = LED - 5mm [color="Red (633nm)" package="5 mm [THT]"]
  LED22 = LED - 5mm [color="Red (633nm)" package="5 mm [THT]"]
  LED23 = LED - 5mm [color="Red (633nm)" package="5 mm [THT]"]
  LED24 = LED - 5mm [color="Red (633nm)" package="5 mm [THT]"]
  LED25 = LED - 5mm [color="Red (633nm)" package="5 mm [THT]"]
  LED3 = LED - 5mm [color="Red (633nm)" package="5 mm [THT]"]

nets:
  N1: LED1.cathode, LED2.cathode, Part1.GND, LED4.cathode, LED5.cathode, LED6.cathode, LED7.cathode, LED8.cathode, LED9.cathode, LED10.cathode, LED11.cathode, LED12.cathode, LED13.cathode, LED14.cathode, LED15.cathode, LED16.cathode, LED17.cathode, LED18.cathode, LED19.cathode, LED3.cathode
  N2: LED1.anode, Part1.D42
  N3: LED2.anode, Part1.D37
  N4: Part1.D22, LED5.anode
  N5: Part1.D23, LED7.anode
  N6: Part1.D24, LED14.anode
  N7: Part1.D25, LED15.anode
  N8: Part1.D26, LED21.anode
  N9: Part1.D27, LED4.anode
  N10: Part1.D28, LED6.anode
  N11: Part1.D29, LED12.anode
  N12: Part1.D30, LED11.anode
  N13: Part1.D31, LED22.anode
  N14: Part1.D32, LED3.anode
  N15: Part1.D33, LED10.anode
  N16: Part1.D34, LED20.anode
  N17: Part1.D35, LED19.anode
  N18: Part1.D36, LED25.anode
  N19: Part1.D38, LED9.anode
  N20: Part1.D39, LED17.anode
  N21: Part1.D40, LED18.anode
  N22: Part1.D41, LED24.anode
  N23: Part1.D43, LED8.anode
  N24: Part1.D44, LED16.anode
  N25: Part1.D45, LED13.anode
  N26: Part1.D53, LED23.anode

notes:
  1 2 3 A
  4 5 6 B
  7 8 9 C
  * 0 # D
  Sajonia, Axl John BSCpE - 1B
